# Fritzing sketch photon_walkie_talkies (saved by Fritzing 0.9.1b)
breadboards: 1

parts:
  Part2 = Mono 2.5W Class D Audio Amplifier - PAM8302  # not connected
  MIC1 = MAX4466 Electret Microphone Breakout Board
  Part3 = Photon
  S1 = Momentary Switch [package=ksa_sealed_tac_switch]
  SPKR1 = Loudspeaker  # not connected

nets:
  N1: MIC1.out, Part3.DAC
  GND: MIC1.GND, Part3.GND
  VCC: MIC1.VCC, Part3.A0, Part3.3V3, S1.2, S1.4
  N2: S1.1, S1.3

custom parts:
  Mono 2.5W Class D Audio Amplifier - PAM8302: A super small but powerful mono amplifier able to deliver up to 2.5 Watts into 4-8 ohm impedance speakers. Inside the miniature chip is a class D controller, able to run from 2.0V-5.5VDC. Since the amp is a class D, its very efficient (over 90% efficient when driving an 8Ω speaker at over half a Watt) - making it perfect for portable and battery-powered projects.
  MAX4466 Electret Microphone Breakout Board: MAX4466 Electrec Microphone Breakout Board
